# Fritzing sketch archi (saved by Fritzing 0.9.10b)
breadboards: 1

parts:
  부품1 = Arduino Uno (Rev3)
  SparkFun_Qwiic_6DoF_LSM6DSO1 = SparkFun Qwiic 6DoF LSM6DSO  # not connected
  R1 = Resistor [tolerance=±5% power=0.25 resistance=10k package=THT]
  S1 = Pushbutton [package="[THT]"]
  Lilypad_Vibe2 = Lilypad Vibe Motor

nets:
  N1: 부품1.D3_PWM, Lilypad_Vibe2.Supply
  N2: 부품1.D4, R1.Pin_1, S1.Pin_1, S1.Pin_2
  N3: 부품1.5V, R1.Pin_0
  GND: 부품1.GND, S1.Pin_3, S1.Pin_4, Lilypad_Vibe2.GND

custom parts:
  SparkFun Qwiic 6DoF LSM6DSO: The SparkFun LSM6DSO 6 Degrees of Freedom Breakout is an accelerometer and gyroscope sensor with a giant 9kB FIFO buffer and embedded processing interrupt functions. Due to the capabilities and low cost of the LSM6DSO we've created this small breakout board just for you! Each LSM6DSO breakout has been designed to be super-flexible and can be configured specifically for many applications. With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
